// Logisim project project a.circ as structural Verilog: 1 circuit, main circuit main
module main (
  input  in_1,
  input  in_2,
  input  in_3,
  input  in_4,
  input  in_5,
  input  in_6,
  output out_7,
  output out_8,
  output out_9
);

  wire and_1_out, button_1_out, button_2_out, d_ff_1_q, d_ff_2_q, d_ff_3_q, d_ff_4_q, d_ff_5_q, d_ff_6_q,
       d_ff_7_q, d_ff_8_q, d_ff_8_qn, d_ff_9_q, not_1_out, not_2_out, or_1_out, or_2_out, XB_2_out, XB_out,
       XB_prime_out, xnor_1_out, xnor_2_out, xnor_3_out;

  not not_1 (not_1_out, and_1_out);
  Button button_1 (.out(button_1_out));
  D_Flip_Flop d_ff_1 (.clk(button_1_out), .D(in_1), .Q(d_ff_1_q), .reset(button_2_out));  // open: Qn, preset, en
  D_Flip_Flop d_ff_2 (.clk(button_1_out), .D(in_2), .Q(d_ff_2_q), .reset(button_2_out));  // open: Qn, preset, en
  D_Flip_Flop d_ff_3 (.clk(button_1_out), .D(in_3), .Q(d_ff_3_q), .reset(button_2_out));  // open: Qn, preset, en
  D_Flip_Flop d_ff_4 (.clk(button_1_out), .D(in_4), .Q(d_ff_4_q), .reset(button_2_out));  // open: Qn, preset, en
  xnor xnor_1 (xnor_1_out, d_ff_1_q, d_ff_4_q);
  D_Flip_Flop d_ff_5 (.clk(button_1_out), .D(in_5), .Q(d_ff_5_q), .reset(button_2_out));  // open: Qn, preset, en
  D_Flip_Flop d_ff_6 (.clk(button_1_out), .D(in_6), .Q(d_ff_6_q), .reset(button_2_out));  // open: Qn, preset, en
  and XB (XB_out, d_ff_7_q, not_1_out);
  and XB_2 (XB_2_out, not_1_out, d_ff_8_q);
  and XB_prime (XB_prime_out, not_1_out, d_ff_8_qn);
  xnor xnor_2 (xnor_2_out, d_ff_2_q, d_ff_5_q);
  xnor xnor_3 (xnor_3_out, d_ff_3_q, d_ff_6_q);
  D_Flip_Flop d_ff_7 (.clk(button_1_out), .D(or_1_out), .Q(d_ff_7_q), .reset(button_2_out));  // open: Qn, preset, en
  or or_1 (or_1_out, XB_out, XB_2_out);
  D_Flip_Flop d_ff_8 (
    .clk(button_1_out), .D(or_2_out), .Q(d_ff_8_q), .Qn(d_ff_8_qn), .reset(button_2_out));  // open: preset, en
  or or_2 (or_2_out, XB_out, XB_prime_out);
  and and_1 (and_1_out, xnor_1_out, xnor_2_out, xnor_3_out);
  or or_3 (out_9, d_ff_9_q, XB_out);
  D_Flip_Flop d_ff_9 (.clk(button_1_out), .D(out_9), .Q(d_ff_9_q), .reset(button_2_out));  // open: Qn, preset, en
  Button button_2 (.out(button_2_out));
  and and_2 (out_7, and_1_out, not_2_out);
  not not_2 (not_2_out, out_9);
  nor nor_1 (out_8, and_1_out, out_9);
endmodule
